// Logisim project circuitoSIMP6.circ as structural Verilog: 1 circuit, main circuit main
module main (
  input  x,
  input  y,
  input  w,
  input  z,
  input  x_2,
  input  y_2,
  input  w_2,
  input  z_2,
  output out_9,
  output out_10
);

  wire and_1_out, and_2_out, and_3_out, not_1_out, not_2_out, not_3_out, not_4_out, not_5_out, not_6_out,
       not_7_out, not_8_out, not_9_out, not_10_out, or_1_out, or_2_out, or_3_out;

  not not_1 (not_1_out, w_2);
  not not_2 (not_2_out, y_2);
  not not_3 (not_3_out, y);
  or or_1 (or_1_out, not_3_out, w, not_4_out);
  not not_4 (not_4_out, x);
  and and_1 (and_1_out, y, not_5_out, x);
  not not_5 (not_5_out, w);
  and and_2 (and_2_out, z, w, y);
  not not_6 (not_6_out, x);
  not not_7 (not_7_out, z_2);
  not not_8 (not_8_out, or_1_out);
  not not_9 (not_9_out, and_1_out);
  or or_2 (or_2_out, and_2_out, not_6_out);
  not not_10 (not_10_out, or_2_out);
  or or_3 (or_3_out, not_7_out, not_1_out, not_2_out);
  and and_3 (and_3_out, not_8_out, not_9_out);
  or or_4 (out_9, and_3_out, not_10_out);
  and and_4 (out_10, or_3_out, x_2);

  // Notes on the sheet:
  //   Circuito efetivamente simplificado
  //   Montando circuito para descobrir a tabela verdade
endmodule
