// Logisim project circuitoSIMP7.circ as structural Verilog: 1 circuit, main circuit main
module main (
  input  x,
  input  y,
  input  z,
  output out_4
);

  wire not_1_out, not_2_out, not_3_out, or_1_out, or_2_out;

  not not_1 (not_1_out, x);
  or or_1 (or_1_out, y, not_1_out);
  not not_2 (not_2_out, z);
  not not_3 (not_3_out, y);
  or or_2 (or_2_out, not_2_out, not_3_out, x);
  and and_1 (out_4, or_1_out, or_2_out);

  // Notes on the sheet:
  //    Circuito referente a expressão simplificada 
endmodule
